# Fritzing sketch weather display (saved by Fritzing 1.0.6)

parts:
  U1 = LuaNode32 / ESP32 [part_number=ESP32S-PIN30]
  Part1 = TFT 2.2 inch 320x240 w microSD [part_number=1480]

nets:
  N1: U1.D32, Part1.BACKLIGHT
  N2: U1.D33, Part1.RESET
  N3: U1.D27, Part1.DC
  GND: U1.GND, Part1.GND
  3V3: U1.3V3, Part1.VIN
  N4: U1.D5, Part1.LCDCS
  N5: U1.D18, Part1.SCLK
  N6: U1.D19, Part1.MISO
  N7: U1.D23, Part1.MOSI

custom parts:
  LuaNode32 / ESP32: New Image for LuaNode32 DOIT ESP32 DEVKIT V1. Base parts from LuaNode32 / ESP32 ESP32 based LuaNode32 by G.Noorlander DOIT Esp32 DevKit v1 (30 pins long, 11 pins width) by Werner Rothschopf (modified by vanepp Dec 2018)
  TFT 2.2 inch 320x240 w microSD: This lovely little display breakout is the best way to add a small, colorful and bright display to any project. Since the display uses 4-wire SPI to communicate and has its own pixel-addressable frame buffer, it can be used with every kind of microcontroller. Even a very small one with low memory and few pins available! The 2.2" display has 320x240 color pixels.
